# Fritzing sketch keyes-relay_arduino (saved by Fritzing 0.8.7b)
breadboards: 1

parts:
  Part1 = Arduino Uno (Rev3)
  KY-1 = Keyes Relay [package=THT]

nets:
  N1: Part1.D10_PWM/SS, KY-1.signal
  N2: Part1.5V, KY-1.power
  N3: Part1.GND, KY-1.ground

custom parts:
  Keyes Relay: The Keyes 5V relay module is suitable for SCM development, home appliance control. It uses a 5V~12V TIL control signal which can control DC / AC signal.
