# Fritzing sketch keyes-tilt-switch_arduino (saved by Fritzing 0.8.7b)
breadboards: 1

parts:
  U1 = Keyes Tilt Switch [package=THT]
  Part1 = Arduino Uno (Rev3)

nets (from the breadboard view):
  N1: U1.signal, Part1.D7
  N2: U1.power, Part1.5V
  N3: U1.ground, Part1.GND

custom parts:
  Keyes Tilt Switch: Keyes Tilt Switch Sensor Module for Arduino (Works with Official Arduino Boards). Working voltage: 3.3V~5V; digital switch output (0 & 1); High sensitivity.
